# Fritzing sketch nodemcu (saved by Fritzing 0.9.3b)

parts:
  U1 = NodeMCU V1.0
  DHT1 = DHT22 Humidity and Temperature Sensor
  Part1 = HC-SR501 Body Sensor Module
  GY-1 = GY-302 [part_number=GY-302]
  KY-1 = Keyes Relay [package=THT]

nets:
  N1: U1.D1, GY-1.SDA
  N2: U1.D2, GY-1.SCL
  N3: U1.D4, DHT1.DATA
  3V3: U1.3V3, DHT1.VDD, GY-1.VCC
  GND: U1.GND, DHT1.GND, Part1.GND, GY-1.ADDR, GY-1.GND, KY-1.ground
  N4: U1.D5, KY-1.signal
  N5: U1.D6, Part1.OUT
  VIN: U1.Vin, Part1.VCC, KY-1.power

custom parts:
  NodeMCU V1.0: ESP9266 based NodeMCU
  HC-SR501 Body Sensor Module: Pyroelectric Infrared PIR Motion Sensor Detector Module
  Keyes Relay: The Keyes 5V relay module is suitable for SCM development, home appliance control. It uses a 5V~12V TIL control signal which can control DC / AC signal.
